// Logisim project OSI630.circ as structural Verilog
module main (
  input  CD0,
  input  CD1,
  input  CD2,
  input  CD3,
  input  PIXEL,
  input  DB
);

  wire nand_4_out, nand_5_out, nand_6_out, nand_7_out, nand_8_out, nand_9_out, nand_10_out, nand_11_out,
       nand_12_out, nand_13_out, nand_14_out, nand_15_out, nBG000, nCD1, nCD2, nCD3, nFG000, nSVID,
       pull_resistor_1_node, pull_resistor_2_node, pull_resistor_3_node, SVID, VID1;

  xor xor_1 (VID1, PIXEL, CD0);
  not not_1 (nCD1, CD1);
  not not_2 (nCD2, CD2);
  not not_3 (nCD3, CD3);
  not not_4 (SVID, nSVID);
  nand nand_1 (nSVID, VID1, DB);
  nand nand_2 (nFG000, nCD1, nCD2, nCD3, SVID);
  nand nand_3 (nBG000, nCD1, nCD2, nCD3, nSVID);
  nand nand_4 (nand_4_out, nBG000, 1'b1, CD1);
  nand nand_5 (nand_5_out, CD1, SVID);
  nand nand_6 (nand_6_out, nBG000, 1'b1, CD2);
  nand nand_7 (nand_7_out, CD2, SVID);
  nand nand_8 (nand_8_out, nBG000, 1'b1, CD3);
  nand nand_9 (nand_9_out, CD3, SVID);
  OC_symbol oc_symbol_1 ();
  nand nand_10 (nand_10_out, nand_4_out, nFG000);
  nand nand_11 (nand_11_out, nand_5_out, nFG000);
  OC_symbol oc_symbol_2 ();
  nand nand_12 (nand_12_out, nand_6_out, nFG000);
  OC_symbol oc_symbol_3 ();
  OC_symbol oc_symbol_4 ();
  nand nand_13 (nand_13_out, nand_7_out, nFG000);
  OC_symbol oc_symbol_5 ();
  nand nand_14 (nand_14_out, nand_8_out, nFG000);
  nand nand_15 (nand_15_out, nand_9_out, nFG000);
  OC_symbol oc_symbol_6 ();
  Pull_Resistor #(.pull(1)) pull_resistor_1 (.node(pull_resistor_1_node));
  LED led_1 (.in(pull_resistor_1_node));
  Pull_Resistor #(.pull(1)) pull_resistor_2 (.node(pull_resistor_2_node));
  LED led_2 (.in(pull_resistor_2_node));
  Pull_Resistor #(.pull(1)) pull_resistor_3 (.node(pull_resistor_3_node));
  LED led_3 (.in(pull_resistor_3_node));

  // Other names for the same wires on the sheet: VID = PIXEL

  // Notes on the sheet:
  //   630
  //   pin 5 is unconnected
  //   74LS means floating high
  //   600
  //   when zero, outputs are always pulled low
  //   TO 630
  //    Schematic seems to have the wrong symbol
  //   LS10 is a quad 3-input NAND, not AND
  //   nand_10 drives only 0 and floats otherwise
  //   nand_11 drives only 0 and floats otherwise
  //   nand_12 drives only 0 and floats otherwise
  //   nand_13 drives only 0 and floats otherwise
  //   nand_14 drives only 0 and floats otherwise
  //   nand_15 drives only 0 and floats otherwise
  //   R
  //   G
  //   B
  //   each output pulls low
  //   or is floating
  //   resistors form voltage
  //   dividers that determine
  //   the intensity and black level
  //   (test, connect for binary RGB)
endmodule
